# Fritzing sketch Untitled Sketch (saved by Fritzing 0.9.3b)
breadboards: 1

parts:
  Composant1 = Arduino Nano (Rev3.0)
  Grove1 = Grove OLED 128x96
  S1 = Pushbutton [package="[THT]"]
  S2 = Pushbutton [package="[THT]"]
  R1 = Resistor [tolerance=±5% resistance=220 package=THT]
  R2 = Resistor [tolerance=±5% resistance=220 package=THT]
  T1 = TMP36 Temperature Sensor [package="TO92 [THT]"]

nets:
  GND: Composant1.GND, Grove1.GND, R1.Pin_1, R2.Pin_1, T1.GND
  N1: Composant1.D2, S1.Pin_3, S1.Pin_4, R2.Pin_0
  N2: Composant1.D3, S2.Pin_3, S2.Pin_4, R1.Pin_0
  N3: Composant1.D8, T1.Vout
  VIN: Composant1.VIN, Grove1.VCC, S1.Pin_1, S1.Pin_2, S2.Pin_1, S2.Pin_2, T1.+Vs
  N4: Composant1.A5, Grove1.SDA
  N5: Composant1.A4, Grove1.SCL

// code stored in the sketch: projet_temp_rature_oled.ino
// Pour le senseur de température
#include <OneWire.h>
#include <DallasTemperature.h>

// Pour l'écran OLED
#include "U8glib.h"

#define ONE_WIRE_BUS 8
#define UP_PIN 2
#define DOWN_PIN 3

const int debounceTime = 500;

const int temperatureDelay = 5; // Temps en secondes
const float maxTemp = 16.0;
const float minTemp = 4.0;
const float tempInterval = 0.5;

OneWire oneWire(ONE_WIRE_BUS);
DallasTemperature sensors(&oneWire);

U8GLIB_SSD1306_128X64 display(U8G_I2C_OPT_NONE);

float desired_temperature = 6.0;

void setup(void) {
  Serial.begin(9600);

  sensors.begin();
  attachInterrupt(digitalPinToInterrupt(UP_PIN), tempUp, RISING);
  attachInterrupt(digitalPinToInterrupt(DOWN_PIN), tempDown, RISING);
}

void loop(void) {
  display.firstPage();

  do {
    display.setFont(u8g_font_gdr14r);
    display.drawStr(0, 16, dtostrf(desired_temperature, 6, 1, "     "));

    display.setFont(u8g_font_gdb30r);
    display.drawStr(0, 55, dtostrf(getTemperature(), 5, 2, "    "));

  } while ( display.nextPage() );
}

void tempUp() {
  static long last_millis;

  if (millis() - last_millis > debounceTime) {
    desired_temperature += tempInterval;
    if (desired_temperature > maxTemp) {
      desired_temperature = maxTemp;
    }
    last_millis = millis();
  }
}

void tempDown() {
  static long last_millis;

  if (millis() - last_millis > debounceTime) {
    desired_temperature -= tempInterval;
    if (desired_temperature < minTemp) {
      desired_temperature = minTemp;
    }
    last_millis = millis();
  }
}

static inline float getTemperature() {
  static unsigned long lastMillis;
  static float temperature = 0;

  unsigned long now = millis();
  if (now - lastMillis >= temperatureDelay * 1000) {
    lastMillis = now;
    sensors.requestTemperatures();
    temperature = sensors.getTempCByIndex(0);
  }
  return temperature;
}
